# Fritzing sketch indicatie (saved by Fritzing 0.9.9b)
breadboards: 1

parts:
  Part2 = Bluetooth HC-05 Macho
  X2 = DB25 [package=db25]
  NEOPIXEL1 = Neopixel Strip -- Black (30/m) [part_number=1376]
  NEOPIXEL2 = Neopixel Strip -- Black (30/m) [part_number=1376]
  Onderdeel1 = Arduino Uno (Rev3) - ICSP
  R1 = Resistor [tolerance=±5% power=0.25 resistance=470 package=THT]
  R2 = Resistor [tolerance=±5% power=0.25 resistance=470 package=THT]

nets:
  N1: Part2.TXD, Onderdeel1.D0/RX
  N2: Part2.RXD, Onderdeel1.D1/TX
  VCC: Part2.VCC, Onderdeel1.5V
  GND: Part2.GND, Onderdeel1.GND
  N3: X2.10, Onderdeel1.A0
  N4: X2.11, Onderdeel1.A1
  N5: X2.12, Onderdeel1.A2
  N6: X2.13, Onderdeel1.D2
  N7: X2.14, Onderdeel1.D3_PWM
  N8: X2.15, Onderdeel1.D4
  N9: X2.16, Onderdeel1.D5_PWM
  N10: X2.17, Onderdeel1.D6_PWM
  N11: X2.18, Onderdeel1.D7
  N12: X2.19, Onderdeel1.D8
  N13: X2.20, Onderdeel1.D9_PWM
  N14: X2.21, Onderdeel1.D10_PWM/SS
  N15: NEOPIXEL1.Din, R2.Pin_1
  N16: NEOPIXEL2.Din, R1.Pin_1
  N17: Onderdeel1.D11_PWM/MOSI, R2.Pin_0
  N18: Onderdeel1.D12/MISO, R1.Pin_0

notes:
  Led Matrix Connector
  HC-02 Bluetooth module
  WS2812B ledstrip

custom parts:
  Neopixel Strip -- Black (30/m): These NeoPixel strips have 30 digitally-addressable pixel LEDs per meter and are very affordable and are only 12.5 mm wide, 10 mm if you remove the strip from the casing.
