# Fritzing sketch remote (saved by Fritzing 0.9.9b)
breadboards: 1

parts:
  Part1 = Arduino Nano (Rev3.0)
  DigitalPushButtonV1 = DigitalPushButtonV2
  DigitalPushButtonV2 = DigitalPushButtonV2
  Part2 = Bluetooth HC-05 Macho
  Part3 = OLED Monochrome 128x32 I2C [part_number=931]

nets:
  N1: Part1.D1/TX, Part2.RXD
  N2: Part1.D0/RX, Part2.TXD
  N3: Part1.D2, DigitalPushButtonV1.Input
  N4: Part1.D3, DigitalPushButtonV2.Input
  GND: Part1.GND, DigitalPushButtonV1.GND, DigitalPushButtonV2.GND, Part2.GND
  5V: Part1.5V, DigitalPushButtonV1.Signal, DigitalPushButtonV2.Signal, Part2.VCC
  N5: Part1.A5, Part3.SCL
  N6: Part1.A4, Part3.SDA

custom parts:
  OLED Monochrome 128x32 I2C: These displays are small, only about 1" diagonal, but very readable due to the high contrast of an OLED display. This display is made of 128x32 individual white OLED pixels, each one is turned on or off by the controller chip. Because the display makes its own light, no backlight is required. This reduces the power required to run the OLED and is why the display has such high contrast; we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
